// Logisim project 1.circ as structural Verilog: 3 circuits, main circuit alu8
module alu8 (
  input  [11:0] a,
  input  [11:0] b,
  input  [3:0] op,
  input  sysclock,
  output [11:0] alur
);

  wire addsub_1_carry, addsub_1_overflow, and_3_out, and_4_out, and_5_out, ca, comparator_1_eq, msk,
       multiplexer_3_out, ovff, zero;
  wire [0:0] op_t;
  wire [2:0] register_1_q;
  wire [11:0] addsub_1_sum, and_7_out, multiplexer_1_out, not_1_out, or_2_out, shifter_1_out, shifter_2_out,
       xor_1_out;

  and and_1 (ovff, msk, addsub_1_overflow);
  and and_2 (ca, msk, addsub_1_carry);
  assign not_1_out = ~a;  // NOT_Gate not_1, 12 bits wide
  Multiplexer #(.width(12), .enable("false")) multiplexer_1 (
    .in0({12{1'b0}}), .in1(12'h1), .out(multiplexer_1_out), .sel(comparator_1_eq));
  Comparator #(.width(12)) comparator_1 (.a(a), .b(b), .eq(comparator_1_eq));  // open: gt, lt
  Shifter #(.width(12)) shifter_1 (.in(a), .\dist (4'b0001), .out(shifter_1_out));
  Shifter #(.width(12), .shift("lr")) shifter_2 (.in(a), .\dist (4'b0001), .out(shifter_2_out));
  and and_3 (and_3_out, ~op[2], op[0]);  // AND_Gate
  and and_4 (and_4_out, op[1], op[0]);
  and and_5 (and_5_out, op[3], op[0]);
  and and_6 (msk, ~op[3], op[2], ~op[1]);  // AND_Gate
  or or_1 (op_t[0], and_3_out, and_4_out, and_5_out);
  assign and_7_out = a & b;  // AND_Gate and_7, 12 bits wide
  assign xor_1_out = a ^ b;  // XOR_Gate xor_1, 12 bits wide
  assign or_2_out = a | b;  // OR_Gate or_2, 12 bits wide
  addsub addsub_1 (
    .inputa(a), .inputb(b), .mode(op[0]), .sum(addsub_1_sum), .overflow(addsub_1_overflow),
    .carry(addsub_1_carry));
  Multiplexer #(.select(4), .width(12), .enable("false")) multiplexer_2 (
    .in0(not_1_out), .in1(and_7_out), .in2(xor_1_out), .in3(or_2_out), .in4(addsub_1_sum), .in6(a),
    .in7({{9{1'b0}}, register_1_q}), .in9(b), .in10(multiplexer_1_out), .in12(shifter_1_out),
    .in13(shifter_2_out), .out(alur), .sel({op[3:1], op_t[0]}));  // open: in5, in8, in11, in14, in15
  Register #(.width(3)) register_1 (
    .D({ovff, ca, zero}), .en(multiplexer_3_out), .clk(sysclock), .Q(register_1_q));  // open: clr
  Multiplexer #(.select(4), .enable("false")) multiplexer_3 (
    .in0(1'b1), .in1(1'b1), .in2(1'b1), .in3(1'b1), .in4(1'b1), .in5(1'b1), .in6(1'b0), .in7(1'b0),
    .in8(1'b0), .in9(1'b0), .in10(1'b1), .in11(1'b0), .in12(1'b1), .in13(1'b1), .in14(1'b0), .in15(1'b0),
    .out(multiplexer_3_out), .sel({op[3:1], op_t[0]}));
  nor nor_1 (zero, alur[0], alur[1], alur[2], alur[3], alur[4], alur[5], alur[6], alur[7], alur[8], alur[9], alur[10], alur[11]);

  // Other names for the same wires on the sheet: clk = sysclock; f0 = op[0]; s0 = op_t[0]; f1 = op[1];
  //   op_t[3:1] = op[3:1]; s1 = op[1]; f2 = op[2]; s2 = op[2]; f3 = op[3]; s3 = op[3]
endmodule

module cla (
  input  [5:0] inputa,
  input  [5:0] inputb,
  input  carryin,
  output [5:0] carryout,
  output [5:0] generator,
  output [5:0] propagator
);

  wire and_7_out, and_8_out, and_9_out, and_10_out, and_11_out, and_12_out, and_13_out, and_14_out,
       and_15_out, and_16_out, and_17_out, and_18_out, and_19_out, and_20_out, and_21_out, and_22_out,
       and_23_out, and_24_out, and_25_out, and_26_out, and_27_out;

  and and_1 (generator[0], inputa[0], inputb[0]);
  and and_2 (generator[1], inputa[1], inputb[1]);
  and and_3 (generator[2], inputa[2], inputb[2]);
  and and_4 (generator[3], inputa[3], inputb[3]);
  and and_5 (generator[4], inputa[4], inputb[4]);
  and and_6 (generator[5], inputa[5], inputb[5]);
  xor xor_1 (propagator[0], inputa[0], inputb[0]);
  xor xor_2 (propagator[1], inputa[1], inputb[1]);
  xor xor_3 (propagator[2], inputa[2], inputb[2]);
  xor xor_4 (propagator[3], inputa[3], inputb[3]);
  xor xor_5 (propagator[4], inputb[4], inputa[4]);
  xor xor_6 (propagator[5], inputa[5], inputb[5]);
  and and_7 (and_7_out, propagator[5], generator[4]);
  and and_8 (and_8_out, propagator[5], propagator[4], generator[3]);
  and and_9 (and_9_out, propagator[5], propagator[4], propagator[3], generator[2]);
  and and_10 (and_10_out, propagator[5], propagator[4], propagator[3], propagator[2], generator[1]);
  and and_11 (and_11_out, propagator[5], propagator[4], propagator[3], propagator[2], propagator[1], generator[0]);
  and and_12 (and_12_out, propagator[5], propagator[4], propagator[3], propagator[2], propagator[1], propagator[0], carryin);
  and and_13 (and_13_out, carryin, propagator[0]);
  and and_14 (and_14_out, propagator[3], generator[2]);
  and and_15 (and_15_out, propagator[3], propagator[2], generator[1]);
  and and_16 (and_16_out, propagator[3], propagator[2], propagator[1], generator[0]);
  and and_17 (and_17_out, propagator[3], propagator[2], propagator[1], propagator[0], carryin);
  or or_1 (carryout[5], generator[5], and_10_out, and_7_out, and_12_out, and_8_out, and_9_out, and_11_out);
  or or_2 (carryout[0], generator[0], and_13_out);
  and and_18 (and_18_out, propagator[1], generator[0]);
  and and_19 (and_19_out, propagator[1], propagator[0], carryin);
  or or_3 (carryout[3], generator[3], and_14_out, and_17_out, and_15_out, and_16_out);
  or or_4 (carryout[1], generator[1], and_18_out, and_19_out);
  and and_20 (and_20_out, propagator[4], generator[3]);
  and and_21 (and_21_out, propagator[4], propagator[3], generator[2]);
  and and_22 (and_22_out, propagator[4], propagator[3], propagator[2], generator[1]);
  and and_23 (and_23_out, propagator[4], propagator[3], propagator[2], propagator[1], generator[0]);
  and and_24 (and_24_out, propagator[4], propagator[3], propagator[2], propagator[1], propagator[0], carryin);
  and and_25 (and_25_out, propagator[2], generator[1]);
  and and_26 (and_26_out, propagator[2], propagator[1], generator[0]);
  and and_27 (and_27_out, propagator[2], propagator[1], propagator[0], carryin);
  or or_5 (carryout[2], generator[2], and_25_out, and_26_out, and_27_out);
  or or_6 (carryout[4], generator[4], and_23_out, and_20_out, and_21_out, and_22_out, and_24_out);

  // Other names for the same wires on the sheet: c0 = carryin; c1 = carryout[0]; cout[5:0] = carryout;
  //   c2 = carryout[1]; c3 = carryout[2]; c4 = carryout[3]; c5 = carryout[4]; c6 = carryout[5]; g[5:0] = generator;
  //   g0 = generator[0]; g1 = generator[1]; g2 = generator[2]; g3 = generator[3]; g4 = generator[4];
  //   g5 = generator[5]; a0 = inputa[0]; a1 = inputa[1]; a2 = inputa[2]; a3 = inputa[3]; a4 = inputa[4];
  //   a5 = inputa[5]; b0 = inputb[0]; b1 = inputb[1]; b2 = inputb[2]; b3 = inputb[3]; b4 = inputb[4]; b5 = inputb[5];
  //   p[5:0] = propagator; p0 = propagator[0]; p1 = propagator[1]; p2 = propagator[2]; p3 = propagator[3];
  //   p4 = propagator[4]; p5 = propagator[5]
endmodule

module addsub (
  input  [11:0] inputa,
  input  [11:0] inputb,
  input  mode,
  output [11:0] sum,
  output overflow,
  output carry
);

  wire last_c1;
  wire [5:1] cla_2_carryout;
  wire [10:6] cla_2_carryout_2;
  wire [11:0] cla_2_propagator, xor_1_out;

  assign xor_1_out = inputb ^ {12{mode}};  // XOR_Gate xor_1, 12 bits wide
  xor xor_2 (overflow, last_c1, carry);
  cla cla_1 (
    .inputa(inputa[11:6]), .inputb(xor_1_out[11:6]), .carryin(cla_2_carryout_2[6]),
    .carryout({carry, last_c1, cla_2_carryout_2[10:7]}), .propagator(cla_2_propagator[11:6]));  // open: generator
  cla cla_2 (
    .inputa(inputa[5:0]), .inputb(xor_1_out[5:0]), .carryin(mode),
    .carryout({cla_2_carryout_2[6], cla_2_carryout}), .propagator(cla_2_propagator[5:0]));  // open: generator
  assign sum = {last_c1, cla_2_carryout_2, cla_2_carryout, mode} ^ cla_2_propagator;  // XOR_Gate xor_3, 12 bits wide

  // Other names for the same wires on the sheet: last_c = carry; s[11:0] = sum
endmodule
