// Logisim project 2.circ as structural Verilog: 3 circuits, main circuit instructions
module instructions (
  input  resetall,
  input  sysclock,
  input  jmp,
  input  [11:0] a,
  output [11:0] pc,
  output [3:0] op,
  output [2:0] rd,
  output [2:0] rs1,
  output [2:0] rs2,
  output [11:0] imm
);

  wire undriven;
  wire [11:0] addr_1_sum, multiplexer_1_out;

  Multiplexer #(.width(12), .enable("false")) multiplexer_1 (
    .in0(addr_1_sum), .in1(a), .out(multiplexer_1_out), .sel(jmp));
  RAM #(.addrWidth(12), .dataWidth(25), .databus("bibus")) ram_1 (
    .addr(pc), .we(1'b0), .oe(1'b1), .clk(sysclock), .dout({op, rd, rs1, rs2, imm}));  // open: din
  Register #(.width(12)) register_1 (.D(multiplexer_1_out), .en(undriven), .clk(sysclock), .Q(pc), .clr(resetall));
  addr addr_1 (.inputa(pc), .inputb({12{1'b0}}), .carryin(1'b1), .sum(addr_1_sum));  // open: overflow, carry
endmodule

module cla (
  input  [5:0] inputa,
  input  [5:0] inputb,
  input  carryin,
  output [5:0] carryout,
  output [5:0] generator,
  output [5:0] propagator
);

  wire and_7_out, and_8_out, and_9_out, and_10_out, and_11_out, and_12_out, and_13_out, and_14_out,
       and_15_out, and_16_out, and_17_out, and_18_out, and_19_out, and_20_out, and_21_out, and_22_out,
       and_23_out, and_24_out, and_25_out, and_26_out, and_27_out;

  and and_1 (generator[0], inputa[0], inputb[0]);
  and and_2 (generator[1], inputa[1], inputb[1]);
  and and_3 (generator[2], inputa[2], inputb[2]);
  and and_4 (generator[3], inputa[3], inputb[3]);
  and and_5 (generator[4], inputa[4], inputb[4]);
  and and_6 (generator[5], inputa[5], inputb[5]);
  xor xor_1 (propagator[0], inputa[0], inputb[0]);
  xor xor_2 (propagator[1], inputa[1], inputb[1]);
  xor xor_3 (propagator[2], inputa[2], inputb[2]);
  xor xor_4 (propagator[3], inputa[3], inputb[3]);
  xor xor_5 (propagator[4], inputb[4], inputa[4]);
  xor xor_6 (propagator[5], inputa[5], inputb[5]);
  and and_7 (and_7_out, propagator[5], generator[4]);
  and and_8 (and_8_out, propagator[5], propagator[4], generator[3]);
  and and_9 (and_9_out, propagator[5], propagator[4], propagator[3], generator[2]);
  and and_10 (and_10_out, propagator[5], propagator[4], propagator[3], propagator[2], generator[1]);
  and and_11 (and_11_out, propagator[5], propagator[4], propagator[3], propagator[2], propagator[1], generator[0]);
  and and_12 (and_12_out, propagator[5], propagator[4], propagator[3], propagator[2], propagator[1], propagator[0], carryin);
  and and_13 (and_13_out, carryin, propagator[0]);
  and and_14 (and_14_out, propagator[3], generator[2]);
  and and_15 (and_15_out, propagator[3], propagator[2], generator[1]);
  and and_16 (and_16_out, propagator[3], propagator[2], propagator[1], generator[0]);
  and and_17 (and_17_out, propagator[3], propagator[2], propagator[1], propagator[0], carryin);
  or or_1 (carryout[5], generator[5], and_10_out, and_7_out, and_12_out, and_8_out, and_9_out, and_11_out);
  or or_2 (carryout[0], generator[0], and_13_out);
  and and_18 (and_18_out, propagator[1], generator[0]);
  and and_19 (and_19_out, propagator[1], propagator[0], carryin);
  or or_3 (carryout[3], generator[3], and_14_out, and_17_out, and_15_out, and_16_out);
  or or_4 (carryout[1], generator[1], and_18_out, and_19_out);
  and and_20 (and_20_out, propagator[4], generator[3]);
  and and_21 (and_21_out, propagator[4], propagator[3], generator[2]);
  and and_22 (and_22_out, propagator[4], propagator[3], propagator[2], generator[1]);
  and and_23 (and_23_out, propagator[4], propagator[3], propagator[2], propagator[1], generator[0]);
  and and_24 (and_24_out, propagator[4], propagator[3], propagator[2], propagator[1], propagator[0], carryin);
  and and_25 (and_25_out, propagator[2], generator[1]);
  and and_26 (and_26_out, propagator[2], propagator[1], generator[0]);
  and and_27 (and_27_out, propagator[2], propagator[1], propagator[0], carryin);
  or or_5 (carryout[2], generator[2], and_25_out, and_26_out, and_27_out);
  or or_6 (carryout[4], generator[4], and_23_out, and_20_out, and_21_out, and_22_out, and_24_out);

  // Other names for the same wires on the sheet: c0 = carryin; c1 = carryout[0]; cout[5:0] = carryout;
  //   c2 = carryout[1]; c3 = carryout[2]; c4 = carryout[3]; c5 = carryout[4]; c6 = carryout[5]; g[5:0] = generator;
  //   g0 = generator[0]; g1 = generator[1]; g2 = generator[2]; g3 = generator[3]; g4 = generator[4];
  //   g5 = generator[5]; a0 = inputa[0]; a1 = inputa[1]; a2 = inputa[2]; a3 = inputa[3]; a4 = inputa[4];
  //   a5 = inputa[5]; b0 = inputb[0]; b1 = inputb[1]; b2 = inputb[2]; b3 = inputb[3]; b4 = inputb[4]; b5 = inputb[5];
  //   p[5:0] = propagator; p0 = propagator[0]; p1 = propagator[1]; p2 = propagator[2]; p3 = propagator[3];
  //   p4 = propagator[4]; p5 = propagator[5]
endmodule

module addr (
  input  [11:0] inputa,
  input  [11:0] inputb,
  input  carryin,
  output [11:0] sum,
  output overflow,
  output carry
);

  wire last_c1;
  wire [5:1] cla_2_carryout;
  wire [10:6] cla_2_carryout_2;
  wire [11:0] cla_2_propagator;

  xor xor_1 (overflow, last_c1, carry);
  cla cla_1 (
    .inputa(inputa[11:6]), .inputb(inputb[11:6]), .carryin(cla_2_carryout_2[6]),
    .carryout({carry, last_c1, cla_2_carryout_2[10:7]}), .propagator(cla_2_propagator[11:6]));  // open: generator
  cla cla_2 (
    .inputa(inputa[5:0]), .inputb(inputb[5:0]), .carryin(carryin),
    .carryout({cla_2_carryout_2[6], cla_2_carryout}), .propagator(cla_2_propagator[5:0]));  // open: generator
  assign sum = {last_c1, cla_2_carryout_2, cla_2_carryout, carryin} ^ cla_2_propagator;  // XOR_Gate xor_2, 12 bits wide

  // Other names for the same wires on the sheet: last_c = carry; s[11:0] = sum
endmodule
