// Logisim project 3.circ as structural Verilog: 1 circuit, main circuit regfile
module regfile (
  input  [2:0] rd,
  input  [11:0] alur,
  input  [11:0] pc,
  input  [11:0] imm,
  input  [3:0] op,
  input  wen,
  input  resetall,
  input  sysclock,
  output [11:0] x0,
  output [11:0] x1,
  output [11:0] x2,
  output [11:0] x3,
  output [11:0] x4,
  output [11:0] x5,
  output [11:0] x6,
  output [11:0] x7
);

  wire decoder_1_out0, decoder_1_out1, decoder_1_out2, decoder_1_out3, decoder_1_out4, decoder_1_out5,
       decoder_1_out6, decoder_1_out7;
  wire [1:0] opp;
  wire [11:0] multiplexer_1_out;

  and and_1 (opp[0], op[3], ~op[2], ~op[1], ~op[0]);  // AND_Gate
  and and_2 (opp[1], op[3], ~op[2], ~op[1], op[0]);  // AND_Gate
  Multiplexer #(.select(2), .width(12), .enable("false")) multiplexer_1 (
    .in0(alur), .in1(pc), .in2(imm), .out(multiplexer_1_out), .sel(opp));  // open: in3
  Decoder #(.select(3)) decoder_1 (
    .out0(decoder_1_out0), .out1(decoder_1_out1), .out2(decoder_1_out2), .out3(decoder_1_out3),
    .out4(decoder_1_out4), .out5(decoder_1_out5), .out6(decoder_1_out6), .out7(decoder_1_out7), .sel(rd),
    .en(wen));
  Register #(.width(12)) register_1 (
    .D(multiplexer_1_out), .en(decoder_1_out0), .clk(sysclock), .Q(x0), .clr(resetall));
  Register #(.width(12)) register_2 (
    .D(multiplexer_1_out), .en(decoder_1_out1), .clk(sysclock), .Q(x1), .clr(resetall));
  Register #(.width(12)) register_3 (
    .D(multiplexer_1_out), .en(decoder_1_out2), .clk(sysclock), .Q(x2), .clr(resetall));
  Register #(.width(12)) register_4 (
    .D(multiplexer_1_out), .en(decoder_1_out3), .clk(sysclock), .Q(x3), .clr(resetall));
  Register #(.width(12)) register_5 (
    .D(multiplexer_1_out), .en(decoder_1_out4), .clk(sysclock), .Q(x4), .clr(resetall));
  Register #(.width(12)) register_6 (
    .D(multiplexer_1_out), .en(decoder_1_out5), .clk(sysclock), .Q(x5), .clr(resetall));
  Register #(.width(12)) register_7 (
    .D(multiplexer_1_out), .en(decoder_1_out6), .clk(sysclock), .Q(x6), .clr(resetall));
  Register #(.width(12)) register_8 (
    .D(multiplexer_1_out), .en(decoder_1_out7), .clk(sysclock), .Q(x7), .clr(resetall));

  // Other names for the same wires on the sheet: f0 = op[0]; f1 = op[1]; f2 = op[2]; f3 = op[3]
endmodule
