// Logisim project 4.circ as structural Verilog: 7 circuits, main circuit cpu
module cpu (
  input  resetall,
  input  sysclock,
  output [11:0] pc,
  output [11:0] x0,
  output [11:0] x1,
  output [11:0] x2,
  output [11:0] x3,
  output [11:0] x4,
  output [11:0] x5,
  output [11:0] x6,
  output [11:0] x7
);

  wire and_1_out, d_ff_1_q, multiplexer_1_out, multiplexer_2_out, not_1_out, not_2_out;
  wire [2:0] instructions_1_rd, instructions_1_rs1, instructions_1_rs2;
  wire [3:0] instructions_1_op;
  wire [11:0] alu8_1_alur, instructions_1_imm, multiplexer_3_out, multiplexer_4_out;

  Multiplexer #(.select(4), .enable("false")) multiplexer_1 (
    .in0(1'b0), .in1(1'b0), .in2(1'b0), .in3(1'b0), .in4(1'b0), .in5(1'b0), .in6(1'b0), .in7(1'b0),
    .in8(1'b0), .in9(1'b0), .in10(1'b0), .in11(1'b1), .in12(1'b0), .in13(1'b0), .in14(1'b0), .in15(1'b0),
    .out(multiplexer_1_out), .sel(instructions_1_op));
  Multiplexer #(.select(4), .enable("false")) multiplexer_2 (
    .in0(1'b0), .in1(1'b0), .in2(1'b0), .in3(1'b0), .in4(1'b0), .in5(1'b0), .in6(1'b0), .in7(1'b0),
    .in8(1'b0), .in9(1'b0), .in10(1'b0), .in11(1'b0), .in12(1'b0), .in13(1'b0), .in14(1'b1), .in15(1'b1),
    .out(multiplexer_2_out), .sel(instructions_1_op));
  D_Flip_Flop d_ff_1 (.clk(sysclock), .Q(d_ff_1_q), .preset(multiplexer_2_out), .reset(resetall));  // open: D, Qn
  instructions instructions_1 (
    .resetall(resetall), .sysclock(sysclock), .jmp(multiplexer_1_out), .a(multiplexer_4_out), .pc(pc),
    .op(instructions_1_op), .rd(instructions_1_rd), .rs1(instructions_1_rs1), .rs2(instructions_1_rs2),
    .imm(instructions_1_imm));
  and and_1 (and_1_out, not_1_out, not_2_out);
  not not_1 (not_1_out, multiplexer_1_out);
  not not_2 (not_2_out, d_ff_1_q);
  regfile regfile_1 (
    .rd(instructions_1_rd), .alur(alu8_1_alur), .pc(pc), .imm(instructions_1_imm), .op(instructions_1_op),
    .wen(and_1_out), .resetall(resetall), .sysclock(sysclock), .x0(x0), .x1(x1), .x2(x2), .x3(x3), .x4(x4),
    .x5(x5), .x6(x6), .x7(x7));
  alu8 alu8_1 (
    .a(multiplexer_4_out), .b(multiplexer_3_out), .op(instructions_1_op), .sysclock(sysclock),
    .alur(alu8_1_alur));
  Multiplexer #(.select(3), .width(12), .enable("false")) multiplexer_3 (
    .in0(x0), .in1(x1), .in2(x2), .in3(x3), .in4(x4), .in5(x5), .in6(x6), .in7(x7), .out(multiplexer_3_out),
    .sel(instructions_1_rs2));
  Multiplexer #(.select(3), .width(12), .enable("false")) multiplexer_4 (
    .in0(x0), .in1(x1), .in2(x2), .in3(x3), .in4(x4), .in5(x5), .in6(x6), .in7(x7), .out(multiplexer_4_out),
    .sel(instructions_1_rs1));

  // Other names for the same wires on the sheet: clk = sysclock
endmodule

module cla (
  input  [5:0] inputa,
  input  [5:0] inputb,
  input  carryin,
  output [5:0] carryout,
  output [5:0] generator,
  output [5:0] propagator
);

  wire and_7_out, and_8_out, and_9_out, and_10_out, and_11_out, and_12_out, and_13_out, and_14_out,
       and_15_out, and_16_out, and_17_out, and_18_out, and_19_out, and_20_out, and_21_out, and_22_out,
       and_23_out, and_24_out, and_25_out, and_26_out, and_27_out;

  and and_1 (generator[0], inputa[0], inputb[0]);
  and and_2 (generator[1], inputa[1], inputb[1]);
  and and_3 (generator[2], inputa[2], inputb[2]);
  and and_4 (generator[3], inputa[3], inputb[3]);
  and and_5 (generator[4], inputa[4], inputb[4]);
  and and_6 (generator[5], inputa[5], inputb[5]);
  xor xor_1 (propagator[0], inputa[0], inputb[0]);
  xor xor_2 (propagator[1], inputa[1], inputb[1]);
  xor xor_3 (propagator[2], inputa[2], inputb[2]);
  xor xor_4 (propagator[3], inputa[3], inputb[3]);
  xor xor_5 (propagator[4], inputb[4], inputa[4]);
  xor xor_6 (propagator[5], inputa[5], inputb[5]);
  and and_7 (and_7_out, propagator[5], generator[4]);
  and and_8 (and_8_out, propagator[5], propagator[4], generator[3]);
  and and_9 (and_9_out, propagator[5], propagator[4], propagator[3], generator[2]);
  and and_10 (and_10_out, propagator[5], propagator[4], propagator[3], propagator[2], generator[1]);
  and and_11 (and_11_out, propagator[5], propagator[4], propagator[3], propagator[2], propagator[1], generator[0]);
  and and_12 (and_12_out, propagator[5], propagator[4], propagator[3], propagator[2], propagator[1], propagator[0], carryin);
  and and_13 (and_13_out, carryin, propagator[0]);
  and and_14 (and_14_out, propagator[3], generator[2]);
  and and_15 (and_15_out, propagator[3], propagator[2], generator[1]);
  and and_16 (and_16_out, propagator[3], propagator[2], propagator[1], generator[0]);
  and and_17 (and_17_out, propagator[3], propagator[2], propagator[1], propagator[0], carryin);
  or or_1 (carryout[5], generator[5], and_10_out, and_7_out, and_12_out, and_8_out, and_9_out, and_11_out);
  or or_2 (carryout[0], generator[0], and_13_out);
  and and_18 (and_18_out, propagator[1], generator[0]);
  and and_19 (and_19_out, propagator[1], propagator[0], carryin);
  or or_3 (carryout[3], generator[3], and_14_out, and_17_out, and_15_out, and_16_out);
  or or_4 (carryout[1], generator[1], and_18_out, and_19_out);
  and and_20 (and_20_out, propagator[4], generator[3]);
  and and_21 (and_21_out, propagator[4], propagator[3], generator[2]);
  and and_22 (and_22_out, propagator[4], propagator[3], propagator[2], generator[1]);
  and and_23 (and_23_out, propagator[4], propagator[3], propagator[2], propagator[1], generator[0]);
  and and_24 (and_24_out, propagator[4], propagator[3], propagator[2], propagator[1], propagator[0], carryin);
  and and_25 (and_25_out, propagator[2], generator[1]);
  and and_26 (and_26_out, propagator[2], propagator[1], generator[0]);
  and and_27 (and_27_out, propagator[2], propagator[1], propagator[0], carryin);
  or or_5 (carryout[2], generator[2], and_25_out, and_26_out, and_27_out);
  or or_6 (carryout[4], generator[4], and_23_out, and_20_out, and_21_out, and_22_out, and_24_out);

  // Other names for the same wires on the sheet: c0 = carryin; c1 = carryout[0]; cout[5:0] = carryout;
  //   c2 = carryout[1]; c3 = carryout[2]; c4 = carryout[3]; c5 = carryout[4]; c6 = carryout[5]; g[5:0] = generator;
  //   g0 = generator[0]; g1 = generator[1]; g2 = generator[2]; g3 = generator[3]; g4 = generator[4];
  //   g5 = generator[5]; a0 = inputa[0]; a1 = inputa[1]; a2 = inputa[2]; a3 = inputa[3]; a4 = inputa[4];
  //   a5 = inputa[5]; b0 = inputb[0]; b1 = inputb[1]; b2 = inputb[2]; b3 = inputb[3]; b4 = inputb[4]; b5 = inputb[5];
  //   p[5:0] = propagator; p0 = propagator[0]; p1 = propagator[1]; p2 = propagator[2]; p3 = propagator[3];
  //   p4 = propagator[4]; p5 = propagator[5]
endmodule

module regfile (
  input  [2:0] rd,
  input  [11:0] alur,
  input  [11:0] pc,
  input  [11:0] imm,
  input  [3:0] op,
  input  wen,
  input  resetall,
  input  sysclock,
  output [11:0] x0,
  output [11:0] x1,
  output [11:0] x2,
  output [11:0] x3,
  output [11:0] x4,
  output [11:0] x5,
  output [11:0] x6,
  output [11:0] x7
);

  wire decoder_1_out0, decoder_1_out1, decoder_1_out2, decoder_1_out3, decoder_1_out4, decoder_1_out5,
       decoder_1_out6, decoder_1_out7;
  wire [1:0] opp;
  wire [11:0] multiplexer_1_out;

  and and_1 (opp[0], op[3], ~op[2], ~op[1], ~op[0]);  // AND_Gate
  and and_2 (opp[1], op[3], ~op[2], ~op[1], op[0]);  // AND_Gate
  Multiplexer #(.select(2), .width(12), .enable("false")) multiplexer_1 (
    .in0(alur), .in1(pc), .in2(imm), .out(multiplexer_1_out), .sel(opp));  // open: in3
  Decoder #(.select(3)) decoder_1 (
    .out0(decoder_1_out0), .out1(decoder_1_out1), .out2(decoder_1_out2), .out3(decoder_1_out3),
    .out4(decoder_1_out4), .out5(decoder_1_out5), .out6(decoder_1_out6), .out7(decoder_1_out7), .sel(rd),
    .en(wen));
  Register #(.width(12)) register_1 (
    .D(multiplexer_1_out), .en(decoder_1_out0), .clk(sysclock), .Q(x0), .clr(resetall));
  Register #(.width(12)) register_2 (
    .D(multiplexer_1_out), .en(decoder_1_out1), .clk(sysclock), .Q(x1), .clr(resetall));
  Register #(.width(12)) register_3 (
    .D(multiplexer_1_out), .en(decoder_1_out2), .clk(sysclock), .Q(x2), .clr(resetall));
  Register #(.width(12)) register_4 (
    .D(multiplexer_1_out), .en(decoder_1_out3), .clk(sysclock), .Q(x3), .clr(resetall));
  Register #(.width(12)) register_5 (
    .D(multiplexer_1_out), .en(decoder_1_out4), .clk(sysclock), .Q(x4), .clr(resetall));
  Register #(.width(12)) register_6 (
    .D(multiplexer_1_out), .en(decoder_1_out5), .clk(sysclock), .Q(x5), .clr(resetall));
  Register #(.width(12)) register_7 (
    .D(multiplexer_1_out), .en(decoder_1_out6), .clk(sysclock), .Q(x6), .clr(resetall));
  Register #(.width(12)) register_8 (
    .D(multiplexer_1_out), .en(decoder_1_out7), .clk(sysclock), .Q(x7), .clr(resetall));

  // Other names for the same wires on the sheet: f0 = op[0]; f1 = op[1]; f2 = op[2]; f3 = op[3]
endmodule

module instructions (
  input  resetall,
  input  sysclock,
  input  jmp,
  input  [11:0] a,
  output [11:0] pc,
  output [3:0] op,
  output [2:0] rd,
  output [2:0] rs1,
  output [2:0] rs2,
  output [11:0] imm
);

  wire d_ff_1_q, multiplexer_2_out, not_1_out;
  wire [11:0] addr_1_sum, multiplexer_1_out;

  Multiplexer #(.width(12), .enable("false")) multiplexer_1 (
    .in0(addr_1_sum), .in1(a), .out(multiplexer_1_out), .sel(jmp));
  RAM #(.addrWidth(12), .dataWidth(25), .databus("bibus")) ram_1 (
    .addr(pc), .we(1'b0), .oe(1'b1), .clk(sysclock), .dout({op, rd, rs1, rs2, imm}));  // open: din
  Register #(.width(12)) register_1 (.D(multiplexer_1_out), .en(not_1_out), .clk(sysclock), .Q(pc), .clr(resetall));
  not not_1 (not_1_out, d_ff_1_q);
  addr addr_1 (.inputa(pc), .inputb({12{1'b0}}), .carryin(1'b1), .sum(addr_1_sum));  // open: overflow, carry
  Multiplexer #(.select(4), .enable("false")) multiplexer_2 (
    .in0(1'b0), .in1(1'b0), .in2(1'b0), .in3(1'b0), .in4(1'b0), .in5(1'b0), .in6(1'b0), .in7(1'b0),
    .in8(1'b0), .in9(1'b0), .in10(1'b0), .in11(1'b0), .in12(1'b0), .in13(1'b0), .in14(1'b0), .in15(1'b1),
    .out(multiplexer_2_out), .sel(op));
  D_Flip_Flop d_ff_1 (.D(multiplexer_2_out), .clk(sysclock), .Q(d_ff_1_q), .reset(resetall));  // open: Qn, preset
endmodule

module addr (
  input  [11:0] inputa,
  input  [11:0] inputb,
  input  carryin,
  output [11:0] sum,
  output overflow,
  output carry
);

  wire last_c1;
  wire [5:1] cla_2_carryout;
  wire [10:6] cla_2_carryout_2;
  wire [11:0] cla_2_propagator;

  xor xor_1 (overflow, last_c1, carry);
  cla cla_1 (
    .inputa(inputa[11:6]), .inputb(inputb[11:6]), .carryin(cla_2_carryout_2[6]),
    .carryout({carry, last_c1, cla_2_carryout_2[10:7]}), .propagator(cla_2_propagator[11:6]));  // open: generator
  cla cla_2 (
    .inputa(inputa[5:0]), .inputb(inputb[5:0]), .carryin(carryin),
    .carryout({cla_2_carryout_2[6], cla_2_carryout}), .propagator(cla_2_propagator[5:0]));  // open: generator
  assign sum = {last_c1, cla_2_carryout_2, cla_2_carryout, carryin} ^ cla_2_propagator;  // XOR_Gate xor_2, 12 bits wide

  // Other names for the same wires on the sheet: last_c = carry; s[11:0] = sum
endmodule

module alu8 (
  input  [11:0] a,
  input  [11:0] b,
  input  [3:0] op,
  input  sysclock,
  output [11:0] alur
);

  wire addsub_1_carry, addsub_1_overflow, and_3_out, and_4_out, and_5_out, ca, comparator_1_eq, msk,
       multiplexer_3_out, ovff, zero;
  wire [0:0] op_t;
  wire [2:0] register_1_q;
  wire [11:0] addsub_1_sum, and_7_out, multiplexer_1_out, not_1_out, or_2_out, shifter_1_out, shifter_2_out,
       xor_1_out;

  and and_1 (ovff, msk, addsub_1_overflow);
  and and_2 (ca, msk, addsub_1_carry);
  assign not_1_out = ~a;  // NOT_Gate not_1, 12 bits wide
  Multiplexer #(.width(12), .enable("false")) multiplexer_1 (
    .in0({12{1'b0}}), .in1(12'h1), .out(multiplexer_1_out), .sel(comparator_1_eq));
  Comparator #(.width(12)) comparator_1 (.a(a), .b(b), .eq(comparator_1_eq));  // open: gt, lt
  Shifter #(.width(12)) shifter_1 (.in(a), .\dist (4'b0001), .out(shifter_1_out));
  Shifter #(.width(12), .shift("lr")) shifter_2 (.in(a), .\dist (4'b0001), .out(shifter_2_out));
  and and_3 (and_3_out, ~op[2], op[0]);  // AND_Gate
  and and_4 (and_4_out, op[1], op[0]);
  and and_5 (and_5_out, op[3], op[0]);
  and and_6 (msk, ~op[3], op[2], ~op[1]);  // AND_Gate
  or or_1 (op_t[0], and_3_out, and_4_out, and_5_out);
  assign and_7_out = a & b;  // AND_Gate and_7, 12 bits wide
  assign xor_1_out = a ^ b;  // XOR_Gate xor_1, 12 bits wide
  assign or_2_out = a | b;  // OR_Gate or_2, 12 bits wide
  addsub addsub_1 (
    .inputa(a), .inputb(b), .mode(op[0]), .sum(addsub_1_sum), .overflow(addsub_1_overflow),
    .carry(addsub_1_carry));
  Multiplexer #(.select(4), .width(12), .enable("false")) multiplexer_2 (
    .in0(not_1_out), .in1(and_7_out), .in2(xor_1_out), .in3(or_2_out), .in4(addsub_1_sum), .in6(a),
    .in7({{9{1'b0}}, register_1_q}), .in9(b), .in10(multiplexer_1_out), .in12(shifter_1_out),
    .in13(shifter_2_out), .out(alur), .sel({op[3:1], op_t[0]}));  // open: in5, in8, in11, in14, in15
  Register #(.width(3)) register_1 (
    .D({ovff, ca, zero}), .en(multiplexer_3_out), .clk(sysclock), .Q(register_1_q));  // open: clr
  Multiplexer #(.select(4), .enable("false")) multiplexer_3 (
    .in0(1'b1), .in1(1'b1), .in2(1'b1), .in3(1'b1), .in4(1'b1), .in5(1'b1), .in6(1'b0), .in7(1'b0),
    .in8(1'b0), .in9(1'b0), .in10(1'b1), .in11(1'b0), .in12(1'b1), .in13(1'b1), .in14(1'b0), .in15(1'b0),
    .out(multiplexer_3_out), .sel({op[3:1], op_t[0]}));
  nor nor_1 (zero, alur[0], alur[1], alur[2], alur[3], alur[4], alur[5], alur[6], alur[7], alur[8], alur[9], alur[10], alur[11]);

  // Other names for the same wires on the sheet: clk = sysclock; f0 = op[0]; s0 = op_t[0]; f1 = op[1];
  //   op_t[3:1] = op[3:1]; s1 = op[1]; f2 = op[2]; s2 = op[2]; f3 = op[3]; s3 = op[3]
endmodule

module addsub (
  input  [11:0] inputa,
  input  [11:0] inputb,
  input  mode,
  output [11:0] sum,
  output overflow,
  output carry
);

  wire last_c1;
  wire [5:1] cla_2_carryout;
  wire [10:6] cla_2_carryout_2;
  wire [11:0] cla_2_propagator, xor_1_out;

  assign xor_1_out = inputb ^ {12{mode}};  // XOR_Gate xor_1, 12 bits wide
  xor xor_2 (overflow, last_c1, carry);
  cla cla_1 (
    .inputa(inputa[11:6]), .inputb(xor_1_out[11:6]), .carryin(cla_2_carryout_2[6]),
    .carryout({carry, last_c1, cla_2_carryout_2[10:7]}), .propagator(cla_2_propagator[11:6]));  // open: generator
  cla cla_2 (
    .inputa(inputa[5:0]), .inputb(xor_1_out[5:0]), .carryin(mode),
    .carryout({cla_2_carryout_2[6], cla_2_carryout}), .propagator(cla_2_propagator[5:0]));  // open: generator
  assign sum = {last_c1, cla_2_carryout_2, cla_2_carryout, mode} ^ cla_2_propagator;  // XOR_Gate xor_3, 12 bits wide

  // Other names for the same wires on the sheet: last_c = carry; s[11:0] = sum
endmodule
